// Logisim project Saper.circ as structural Verilog: 1 circuit, main circuit main
module main (
);

  wire clock_1_out, clock_2_out, Enter, Koniec, M, Reset, Start;
  wire [1:0] DISP, main_3_zegar;
  wire [2:0] uklad_zmiany_sterowania_z_3bit_na_5bit_1_out_x__3bit,
       uklad_zmiany_sterowania_z_3bit_na_5bit_1_out_xy_3bit, W1D, W2D, W3D, W4D;
  wire [3:0] V, W1U, W2U, W3U, W4U;
  wire [4:0] X5, Y5;
  wire [5:0] main_3_dane;
  wire [6:0] Klawiatura;
  wire [24:0] S_25b;
  wire [30:0] main_1_p7, main_1_p8, main_1_p9, main_1_p10, main_1_p11, main_1_p12, main_1_p13, main_1_p14,
       main_1_p15, main_1_p16, main_1_p17, main_1_p18, main_1_p19, main_1_p20, main_1_p21, main_1_p22,
       main_1_p23, main_1_p24, main_1_p25, main_1_p26, main_1_p27, main_1_p28, main_1_p29, main_1_p30,
       main_1_p31, main_1_p32, main_1_p33, main_1_p34, main_1_p35, main_1_p36, main_1_p37;

  Button button_1 (.out(Start));
  Button button_2 (.out(Reset));
  // SAPER2_main main_1: pin names not known; wires that end beside it: X5, Y5, V, Start, S_25b, Enter, main_1_p7, main_1_p8, main_1_p9, main_1_p10, main_1_p11, main_1_p12, main_1_p13, main_1_p14, main_1_p15, main_1_p16, main_1_p17, main_1_p18, main_1_p19, main_1_p20, main_1_p21, main_1_p22, main_1_p23, main_1_p24, main_1_p25, main_1_p26, main_1_p27, main_1_p28, main_1_p29, main_1_p30, main_1_p31, main_1_p32, main_1_p33, main_1_p34, main_1_p35, main_1_p36, main_1_p37
  DotMatrix #(.inputtype("row"), .matrixcols(31), .matrixrows(31)) dotmatrix_1 (
    .row0(main_1_p7), .row1(main_1_p8), .row2(main_1_p9), .row3(main_1_p10), .row4(main_1_p11),
    .row5(main_1_p12), .row6(main_1_p13), .row7(main_1_p14), .row8(main_1_p15), .row9(main_1_p16),
    .row10(main_1_p17), .row11(main_1_p18), .row12(main_1_p19), .row13(main_1_p20), .row14(main_1_p21),
    .row15(main_1_p22), .row16(main_1_p23), .row17(main_1_p24), .row18(main_1_p25), .row19(main_1_p26),
    .row20(main_1_p27), .row21(main_1_p28), .row22(main_1_p29), .row23(main_1_p30), .row24(main_1_p31),
    .row25(main_1_p32), .row26(main_1_p33), .row27(main_1_p34), .row28(main_1_p35), .row29(main_1_p36),
    .row30(main_1_p37));
  Clock clock_1 (.out(clock_1_out));
  Keyboard keyboard_1 (.clk(clock_1_out), .data(Klawiatura));  // open: re, clr, avail
  \Sterowanie_dużo  \sterowanie_dużo_1  (
    .Wejscie_Klawiatury(Klawiatura), .Nr_Zaznaczonego_pola(S_25b), .Enter(Enter), .M(M), .X(X5), .Y(Y5));
  Clock #(.highDuration(32), .lowDuration(32)) clock_2 (.out(clock_2_out));
  licznik_czasu_main main_2 (.CLK(clock_2_out), .Stop(Koniec), .Start(Start), .out_5(DISP));  // open: Czas
  _7_Segment_Display u_7_segment_display_1 (
    .g(W4U[3]), .f(W4U[2]), .a(W4U[1]), .b(W4U[0]), .e(W4D[2]), .d(W4D[1]), .c(W4D[0]));  // open: dp
  _7_Segment_Display u_7_segment_display_2 (
    .g(W3U[3]), .f(W3U[2]), .a(W3U[1]), .b(W3U[0]), .e(W3D[2]), .d(W3D[1]), .c(W3D[0]));  // open: dp
  LED led_1 (.in(1'b1));
  LED led_2 (.in(1'b1));
  _7_Segment_Display u_7_segment_display_3 (
    .g(W2U[3]), .f(W2U[2]), .a(W2U[1]), .b(W2U[0]), .e(W2D[2]), .d(W2D[1]), .c(W2D[0]));  // open: dp
  _7_Segment_Display u_7_segment_display_4 (
    .g(W1U[3]), .f(W1U[2]), .a(W1U[1]), .b(W1U[0]), .e(W1D[2]), .d(W1D[1]), .c(W1D[0]));  // open: dp
  wyswietlacz_czasu wyswietlacz_czasu_1 (
    .DISP_IN__1bit_reset_0bit_clk(DISP), .O3D(W4D), .O2D(W3D), .O1D(W2D), .O0D(W1D), .O3U(W4U), .O2U(W3U),
    .O1U(W2U), .O0U(W1U));
  Maszyna_Los_XY22_main main_3 (.START(Start), .DANE(main_3_dane), .ZEGAR(main_3_zegar));
  Uklad_zmiany_sterowania_z_3bit_na_5bit uklad_zmiany_sterowania_z_3bit_na_5bit_1 (
    .IN_X_5bit(X5), .IN_Y_5bit(Y5), .OUT_X__3bit(uklad_zmiany_sterowania_z_3bit_na_5bit_1_out_x__3bit),
    .OUT_XY_3bit(uklad_zmiany_sterowania_z_3bit_na_5bit_1_out_xy_3bit));
  // porównywacz_main main_4: pin names not known; wires that end beside it: main_3_zegar, main_3_dane, Start, uklad_zmiany_sterowania_z_3bit_na_5bit_1_out_x__3bit, Enter, uklad_zmiany_sterowania_z_3bit_na_5bit_1_out_xy_3bit, V

  // Notes on the sheet:
  //   RESTART NIE DZIALA
  //   CZasami nie wykrywa bomb
  //   Aby rozpocząć rozgrywkę trzeba kliknąć start i poczekać z 3 sekundy aż bomby się ustawią
  //   Symulacja 64Hz
endmodule
