// Logisim project Sterowanie.circ as structural Verilog: 3 circuits, main circuit Sterowanie z klawiatury
module Sterowanie_z_klawiatury (
  input  [6:0] \input ,
  output [2:0] _3_a_4_s_1_d_6_w_5_enter,
  output przemiesc_kursor
);

  wire [4:0] komparator_7bit_do_sterowania_1__1_oznacza_ze_jest_rowne;

  Komparator_7bit_do_sterowania komparator_7bit_do_sterowania_1 (
    .A(\input ), .B(7'b1100001),
    ._1_oznacza_ze_jest_rowne(komparator_7bit_do_sterowania_1__1_oznacza_ze_jest_rowne[0]));
  Komparator_7bit_do_sterowania komparator_7bit_do_sterowania_2 (
    .A(\input ), .B(7'b1110011),
    ._1_oznacza_ze_jest_rowne(komparator_7bit_do_sterowania_1__1_oznacza_ze_jest_rowne[1]));
  Komparator_7bit_do_sterowania komparator_7bit_do_sterowania_3 (
    .A(\input ), .B(7'b1100100),
    ._1_oznacza_ze_jest_rowne(komparator_7bit_do_sterowania_1__1_oznacza_ze_jest_rowne[2]));
  Komparator_7bit_do_sterowania komparator_7bit_do_sterowania_4 (
    .A(\input ), .B(7'b1110111),
    ._1_oznacza_ze_jest_rowne(komparator_7bit_do_sterowania_1__1_oznacza_ze_jest_rowne[3]));
  Komparator_7bit_do_sterowania komparator_7bit_do_sterowania_5 (
    .A(\input ), .B(7'b0001010),
    ._1_oznacza_ze_jest_rowne(komparator_7bit_do_sterowania_1__1_oznacza_ze_jest_rowne[4]));
  or or_1 (przemiesc_kursor, komparator_7bit_do_sterowania_1__1_oznacza_ze_jest_rowne[0], komparator_7bit_do_sterowania_1__1_oznacza_ze_jest_rowne[1], komparator_7bit_do_sterowania_1__1_oznacza_ze_jest_rowne[2], komparator_7bit_do_sterowania_1__1_oznacza_ze_jest_rowne[3]);
  ROM #(.addrWidth(5), .dataWidth(3)) rom_1 (
    .addr(komparator_7bit_do_sterowania_1__1_oznacza_ze_jest_rowne), .data(_3_a_4_s_1_d_6_w_5_enter));  // open: sel

  // Notes on the sheet:
  //   contents of rom_1 (hex, n*v repeats v):
  //   0 3 4 0 1 0 0 0 6 7*0 5
endmodule

module uklad_zwracajacy_pozycje (
  input  [2:0] Sterowanie,
  input  Move,
  output [4:0] Poz_X,
  output [4:0] Poz_Y
);

  wire and_1_out, buffer_1_out, buffer_2_out, buffer_3_out, not_1_out;
  wire [2:0] counter_1_q, counter_2_q;

  not not_1 (not_1_out, Sterowanie[0]);
  buf buffer_1 (buffer_1_out, Sterowanie[1]);
  Counter #(.width(3), .max('h4), .trigger("falling")) counter_1 (
    .load(Sterowanie[1]), .D(counter_1_q), .count(Sterowanie[0]), .Q(counter_1_q), .clk(buffer_2_out));  // open: carry, clr
  buf buffer_2 (buffer_2_out, Move);
  Counter #(.width(3), .max('h4), .trigger("falling")) counter_2 (
    .load(buffer_1_out), .D(counter_2_q), .count(and_1_out), .Q(counter_2_q), .clk(buffer_3_out));  // open: carry, clr
  buf buffer_3 (buffer_3_out, Move);
  and and_1 (and_1_out, not_1_out, Sterowanie[2]);
  Shifter #(.width(5), .shift("rr")) shifter_1 (.in(5'b10000), .\dist (counter_1_q), .out(Poz_X));
  Shifter #(.width(5), .shift("rr")) shifter_2 (.in(5'b10000), .\dist (counter_2_q), .out(Poz_Y));

  // Other names for the same wires on the sheet: Control[2:0] = Sterowanie; M = Move
endmodule

module Uklad_zmiany_sterowania_z_3bit_na_5bit (
  input  [4:0] IN_X_5bit,
  input  [4:0] IN_Y_5bit,
  output [2:0] OUT_X__3bit,
  output [2:0] OUT_XY_3bit
);

  assign OUT_X__3bit = IN_X_5bit[0] ? 3'b100 : 3'bz;  // Controlled_Buffer controlled_buffer_1
  assign OUT_X__3bit = IN_X_5bit[1] ? 3'b011 : 3'bz;  // Controlled_Buffer controlled_buffer_2
  assign OUT_X__3bit = IN_X_5bit[4] ? 3'b000 : 3'bz;  // Controlled_Buffer controlled_buffer_3
  assign OUT_XY_3bit = IN_Y_5bit[0] ? 3'b100 : 3'bz;  // Controlled_Buffer controlled_buffer_4
  assign OUT_XY_3bit = IN_Y_5bit[1] ? 3'b011 : 3'bz;  // Controlled_Buffer controlled_buffer_5
  assign OUT_XY_3bit = IN_Y_5bit[4] ? 3'b000 : 3'bz;  // Controlled_Buffer controlled_buffer_6
  assign OUT_X__3bit = IN_X_5bit[2] ? 3'b010 : 3'bz;  // Controlled_Buffer controlled_buffer_7
  assign OUT_X__3bit = IN_X_5bit[3] ? 3'b001 : 3'bz;  // Controlled_Buffer controlled_buffer_8
  assign OUT_XY_3bit = IN_Y_5bit[2] ? 3'b010 : 3'bz;  // Controlled_Buffer controlled_buffer_9
  assign OUT_XY_3bit = IN_Y_5bit[3] ? 3'b001 : 3'bz;  // Controlled_Buffer controlled_buffer_10
endmodule
