// Logisim project test.circ as structural Verilog: 1 circuit, main circuit main
module main (
);

  wire [1:0] register_1_q;
  wire [2:0] rom_1_data, rom_1_data_2, rom_1_data_3, rom_1_data_4, rom_1_data_5, rom_1_data_6, rom_1_data_7,
       rom_1_data_8, rom_1_data_9;

  Register #(.width(2)) register_1 (.Q(register_1_q));  // open: D, en, clk, clr
  DotMatrix #(.matrixcols(3), .matrixrows(3)) dotmatrix_1 (.col0(rom_1_data_3), .col1(rom_1_data_2), .col2(rom_1_data));
  DotMatrix #(.matrixcols(3), .matrixrows(3)) dotmatrix_2 (
    .col0(rom_1_data_6), .col1(rom_1_data_5), .col2(rom_1_data_4));
  DotMatrix #(.matrixcols(3), .matrixrows(3)) dotmatrix_3 (
    .col0(rom_1_data_9), .col1(rom_1_data_8), .col2(rom_1_data_7));
  ROM #(.addrWidth(2), .dataWidth(27)) rom_1 (
    .addr(register_1_q),
    .data({rom_1_data_9, rom_1_data_8, rom_1_data_7, rom_1_data_6, rom_1_data_5, rom_1_data_4, rom_1_data_3, rom_1_data_2, rom_1_data}));  // open: sel

  // Notes on the sheet:
  //   contents of rom_1 (hex, n*v repeats v):
  //   f f000 f00000
endmodule
